# Fritzing sketch NMEALogger (saved by Fritzing 0.6.3b)

parts:
  Arduino2 = Arduino
  Part2 = MicroSD_Breakout_0544
  Part1 = GPS_LS20031

nets:
  N1: Arduino2.GND, Part2.connector2, Part1.connector10
  N2: Arduino2.D13, Part2.connector3
  N3: Arduino2.D12, Part2.connector1
  N4: Arduino2.D11, Part2.connector5
  N5: Arduino2.D10, Part2.connector6
  N6: Arduino2.D0RX, Part1.connector9
  N7: Arduino2.3V3, Part2.connector4, Part1.connector7
